// Digital circuit controlUnit.dig as structural Verilog
module controlUnit (
  input  [31:0] A,
  input  eq,
  input  lt,
  output [12:0] out,
  output on_off
);

  wire and_1_out, multiplexer_1_out, not_1_out, not_2_out, not_3_out, not_4_out;
  wire [1:0] Branchs_d, OPcode_commander_d;
  wire [2:0] ULA_commander_d;

  not not_1 (not_1_out, eq);
  not not_2 (not_2_out, lt);
  ROM #(.AddrBits(3), .Bits(2)) Branchs (.A(A[14:12]), .sel(1'b1), .D(Branchs_d));
  Multiplexer #(.Selector_Bits(2)) multiplexer_1 (
    .sel(Branchs_d), .in_0(eq), .in_1(not_1_out), .in_2(lt), .in_3(not_2_out), .out(multiplexer_1_out));
  ROM #(.AddrBits(7), .Bits(11)) OPcode_commander (.A(A[6:0]), .sel(1'b1), .D({out[9], out[7:0], OPcode_commander_d}));
  ROM #(.AddrBits(10), .Bits(3)) ULA_commander (.A({A[31:25], A[14:12]}), .sel(1'b1), .D(ULA_commander_d));
  and and_1 (and_1_out, multiplexer_1_out, OPcode_commander_d[1]);
  Multiplexer #(.Bits(3)) multiplexer_2 (.sel(A[4]), .in_0(3'b000), .in_1(ULA_commander_d), .out(out[12:10]));
  or or_1 (out[8], and_1_out, OPcode_commander_d[0]);
  not not_3 (not_3_out, A[0]);
  not not_4 (not_4_out, A[1]);
  and and_2 (on_off, not_3_out, not_4_out);

  // Other names for the same wires on the sheet: OP_code[6:0] = A[6:0]

  // Notes on the sheet:
  //   contents of Branchs (hex, n*v repeats v):
  //   0,1,0,0,2,3
  //   contents of OPcode_commander (hex, n*v repeats v):
  //   0,0,0,254,15*0,240,15*0,c8,15*0,200,47*0,102,0,0,0,661,7*0,3a1
  //   contents of ULA_commander (hex, n*v repeats v):
  //   0,5,6,0,3,0,4,2,248*0,1
endmodule
