// Digital circuit immediateTransformer.dig as structural Verilog
module immediateTransformer (
  input  [1:0] ImmSelec,
  input  [31:0] A,
  output [31:0] \output 
);

  wire [31:0] B_type, I_type, J_type, S_type;

  BitExtender #(.inputBits(12), .outputBits(32)) bitextender_1 (.in(A[31:20]), .out(I_type));
  BitExtender #(.inputBits(12), .outputBits(32)) bitextender_2 (.in({A[31:25], A[11:7]}), .out(S_type));
  BitExtender #(.inputBits(13), .outputBits(32)) bitextender_3 (
    .in({A[31], A[7], A[30:25], A[11:8], 1'b0}), .out(B_type));
  BitExtender #(.inputBits(21), .outputBits(32)) bitextender_4 (
    .in({A[31], A[19:12], A[20], A[30:21], 1'b0}), .out(J_type));
  Multiplexer #(.Bits(32), .Selector_Bits(2)) multiplexer_1 (
    .sel(ImmSelec), .in_0(I_type), .in_1(S_type), .in_2(B_type), .in_3(J_type), .out(\output ));

  // Other names for the same wires on the sheet: _0 = A[0]; _1 = A[1]; _2 = A[2]; _3 = A[3]; _4 = A[4]; _5 = A[5];
  //   _6 = A[6]; _7 = A[7]; _8 = A[8]; _9 = A[9]; _10 = A[10]; _11 = A[11]; _12 = A[12]; _13 = A[13]; _14 = A[14];
  //   _15 = A[15]; _16 = A[16]; _17 = A[17]; _18 = A[18]; _19 = A[19]; _20 = A[20]; _21 = A[21]; _22 = A[22];
  //   _23 = A[23]; _24 = A[24]; _25 = A[25]; _26 = A[26]; _27 = A[27]; _28 = A[28]; _29 = A[29]; _30 = A[30];
  //   _31 = A[31]
endmodule
