// Digital circuit processor.dig as structural Verilog
module processor (
  input  clk
);

  wire B_src, clk_t, controlunit_1_p2, controlunit_1_p3, controlunit_1_p5, hatch_q, RAM_r, RAM_w, W_reg;
  wire [1:0] ImmC, PC_src, Resu_src;
  wire [2:0] ULAc;
  wire [4:0] code_memory_d_2;
  wire [15:0] add_1_s, add_2_s, multiplexer_2_out, PC_q, ula_1_p6;
  wire [31:0] bitextender_1_out, code_memory_d, immediatetransformer_1_output, multiplexer_3_out,
       multiplexer_4_out, ramdualport_1_d, registrador_dois_1_a, registrador_dois_1_b;
  wire [31:16] ula_1_p6_2;

  Multiplexer multiplexer_1 (.sel(hatch_q), .in_0(clk), .in_1(1'b0), .out(clk_t));
  D_FF hatch (.D(controlunit_1_p5), .C(clk_t), .Q(hatch_q));  // open: nQ
  Multiplexer #(.Selector_Bits(2), .Bits(16)) multiplexer_2 (
    .sel(PC_src), .in_0(add_1_s), .in_1(add_2_s), .in_2({16{1'b0}}), .in_3(ula_1_p6), .out(multiplexer_2_out));
  D_FF #(.Bits(16)) PC (.D(multiplexer_2_out), .C(clk_t), .Q(PC_q));  // open: nQ
  Add #(.Bits(16)) add_1 (.a(16'h4), .b(PC_q), .c_i(1'b0), .s(add_1_s));  // open: c_o
  ROM #(.AddrBits(16), .isProgramMemory("true"), .Bits(32)) code_memory (
    .A(PC_q), .sel(1'b1), .D({code_memory_d[31:12], code_memory_d_2, code_memory_d[6:0]}));
  // controlUnit controlunit_1: pin names not known; wires that end beside it: {code_memory_d[31:12], code_memory_d_2, code_memory_d[6:0]}, controlunit_1_p2, controlunit_1_p3, {ULAc, PC_src, W_reg, ImmC, B_src, Resu_src, RAM_w, RAM_r}, controlunit_1_p5
  registrador_dois registrador_dois_1 (
    .rs1(code_memory_d[19:15]), .rs2(code_memory_d[24:20]), .rd(code_memory_d_2), .ula(multiplexer_4_out),
    .ck(clk_t), .W_reg(W_reg), .A(registrador_dois_1_a), .B(registrador_dois_1_b));
  immediateTransformer immediatetransformer_1 (
    .\output (immediatetransformer_1_output), .ImmSelec(ImmC),
    .A({code_memory_d[31:12], code_memory_d_2, code_memory_d[6:0]}));
  BitExtender #(.inputBits(16), .outputBits(32)) bitextender_1 (.in(add_1_s), .out(bitextender_1_out));
  Multiplexer #(.Bits(32)) multiplexer_3 (
    .sel(B_src), .in_0(registrador_dois_1_b), .in_1(immediatetransformer_1_output), .out(multiplexer_3_out));
  Add #(.Bits(16)) add_2 (.a(PC_q), .b(immediatetransformer_1_output[15:0]), .c_i(1'b0), .s(add_2_s));  // open: c_o
  // ula ula_1: pin names not known; wires that end beside it: registrador_dois_1_a, multiplexer_3_out, ULAc, controlunit_1_p2, controlunit_1_p3, {ula_1_p6_2, ula_1_p6}
  RAMDualPort #(.AddrBits(24), .Bits(32)) ramdualport_1 (
    .A({ula_1_p6_2[23:16], ula_1_p6}), .Din(registrador_dois_1_b), .str(RAM_w), .C(clk_t), .ld(RAM_r),
    .D(ramdualport_1_d));
  Multiplexer #(.Selector_Bits(2), .Bits(32)) multiplexer_4 (
    .sel(Resu_src), .in_0({ula_1_p6_2, ula_1_p6}), .in_1(ramdualport_1_d), .in_2(bitextender_1_out),
    .in_3({32{1'b0}}), .out(multiplexer_4_out));

  // Notes on the sheet:
  //   contents of code_memory (hex, n*v repeats v):
  //   413,0,0,0,1400913,0,0,0,100593,0,0,0,100613,0,0,0,12006b3,0,0,0
  //   ,c000ef,0,0,0,a00893,7*0,200493,0,0,0,b42023,0,0,0,c42223,0,0,0
  //   ,2d4d263,0,0,0,249293,0,0,0,8282b3,0,0,0,ffc2a303,0,0,0,ff82a383
  //   ,0,0,0,730e33,0,0,0,1c2a023,0,0,0,148493,0,0,0,fe1ff0ef,0,0,0,80e7
endmodule
