// Digital circuit registrador.dig as structural Verilog
module registrador (
  input  [4:0] rs1,
  input  [4:0] rs2,
  input  [4:0] rd,
  input  [31:0] ula,
  input  ck,
  input  W_reg,
  output [31:0] A,
  output [31:0] B
);

  wire and_1_out, C0, C1, C2, C3, C4, C5, C6, C7, C8, C9, C10, C11, C12, C13, C14, C15, C16, C17, C18, C19,
       C20, C21, C22, C23, C24, C25, C26, C27, C28, C29, C30, C31;
  wire [31:0] _0_q, f1, f2, f3, f4, f5, f6, f7, f8, f9, f10, f11, f12, f13, f14, f15, f16, f17, f18, f19,
       f20, f21, f22, f23, f24, f25, f26, f27, f28, f29, f30, f31;

  and and_1 (and_1_out, W_reg, ck);
  Demultiplexer #(.Selector_Bits(5)) demultiplexer_1 (
    .sel(rd), .in(and_1_out), .out_0(C0), .out_1(C1), .out_2(C2), .out_3(C3), .out_4(C4), .out_5(C5),
    .out_6(C6), .out_7(C7), .out_8(C8), .out_9(C9), .out_10(C10), .out_11(C11), .out_12(C12), .out_13(C13),
    .out_14(C14), .out_15(C15), .out_16(C16), .out_17(C17), .out_18(C18), .out_19(C19), .out_20(C20),
    .out_21(C21), .out_22(C22), .out_23(C23), .out_24(C24), .out_25(C25), .out_26(C26), .out_27(C27),
    .out_28(C28), .out_29(C29), .out_30(C30), .out_31(C31));
  D_FF #(.Bits(32)) _0 (.D(ula), .C(C0), .Q(_0_q));  // open: nQ
  D_FF #(.Bits(32)) _1 (.D(ula), .C(C1), .Q(f1));  // open: nQ
  D_FF #(.Bits(32)) _2 (.D(ula), .C(C2), .Q(f2));  // open: nQ
  D_FF #(.Bits(32)) _3 (.D(ula), .C(C3), .Q(f3));  // open: nQ
  D_FF #(.Bits(32)) _4 (.D(ula), .C(C4), .Q(f4));  // open: nQ
  D_FF #(.Bits(32)) _5 (.D(ula), .C(C5), .Q(f5));  // open: nQ
  D_FF #(.Bits(32)) _6 (.D(ula), .C(C6), .Q(f6));  // open: nQ
  D_FF #(.Bits(32)) _7 (.D(ula), .C(C7), .Q(f7));  // open: nQ
  D_FF #(.Bits(32)) _8 (.D(ula), .C(C8), .Q(f8));  // open: nQ
  D_FF #(.Bits(32)) _9 (.D(ula), .C(C9), .Q(f9));  // open: nQ
  D_FF #(.Bits(32)) _10 (.D(ula), .C(C10), .Q(f10));  // open: nQ
  D_FF #(.Bits(32)) _11 (.D(ula), .C(C11), .Q(f11));  // open: nQ
  D_FF #(.Bits(32)) _12 (.D(ula), .C(C12), .Q(f12));  // open: nQ
  D_FF #(.Bits(32)) _13 (.D(ula), .C(C13), .Q(f13));  // open: nQ
  D_FF #(.Bits(32)) _14 (.D(ula), .C(C14), .Q(f14));  // open: nQ
  D_FF #(.Bits(32)) _15 (.D(ula), .C(C15), .Q(f15));  // open: nQ
  D_FF #(.Bits(32)) _16 (.D(ula), .C(C16), .Q(f16));  // open: nQ
  D_FF #(.Bits(32)) _17 (.D(ula), .C(C17), .Q(f17));  // open: nQ
  D_FF #(.Bits(32)) _18 (.D(ula), .C(C18), .Q(f18));  // open: nQ
  D_FF #(.Bits(32)) _19 (.D(ula), .C(C19), .Q(f19));  // open: nQ
  D_FF #(.Bits(32)) _20 (.D(ula), .C(C20), .Q(f20));  // open: nQ
  D_FF #(.Bits(32)) _21 (.D(ula), .C(C21), .Q(f21));  // open: nQ
  D_FF #(.Bits(32)) _22 (.D(ula), .C(C22), .Q(f22));  // open: nQ
  D_FF #(.Bits(32)) _23 (.D(ula), .C(C23), .Q(f23));  // open: nQ
  D_FF #(.Bits(32)) _24 (.D(ula), .C(C24), .Q(f24));  // open: nQ
  D_FF #(.Bits(32)) _25 (.D(ula), .C(C25), .Q(f25));  // open: nQ
  D_FF #(.Bits(32)) _26 (.D(ula), .C(C26), .Q(f26));  // open: nQ
  D_FF #(.Bits(32)) _27 (.D(ula), .C(C27), .Q(f27));  // open: nQ
  D_FF #(.Bits(32)) _28 (.D(ula), .C(C28), .Q(f28));  // open: nQ
  D_FF #(.Bits(32)) _29 (.D(ula), .C(C29), .Q(f29));  // open: nQ
  D_FF #(.Bits(32)) _30 (.D(ula), .C(C30), .Q(f30));  // open: nQ
  D_FF #(.Bits(32)) _31 (.D(ula), .C(C31), .Q(f31));  // open: nQ
  Multiplexer #(.Selector_Bits(5), .Bits(32)) multiplexer_1 (
    .sel(rs1), .in_0({32{1'b0}}), .in_1(f1), .in_2(f2), .in_3(f3), .in_4(f4), .in_5(f5), .in_6(f6),
    .in_7(f7), .in_8(f8), .in_9(f9), .in_10(f10), .in_11(f11), .in_12(f12), .in_13(f13), .in_14(f14),
    .in_15(f15), .in_16(f16), .in_17(f17), .in_18(f18), .in_19(f19), .in_20(f20), .in_21(f21), .in_22(f22),
    .in_23(f23), .in_24(f24), .in_25(f25), .in_26(f26), .in_27(f27), .in_28(f28), .in_29(f29), .in_30(f30),
    .in_31(f31), .out(A));
  Multiplexer #(.Selector_Bits(5), .Bits(32)) multiplexer_2 (
    .sel(rs2), .in_0({32{1'b0}}), .in_1(f1), .in_2(f2), .in_3(f3), .in_4(f4), .in_5(f5), .in_6(f6),
    .in_7(f7), .in_8(f8), .in_9(f9), .in_10(f10), .in_11(f11), .in_12(f12), .in_13(f13), .in_14(f14),
    .in_15(f15), .in_16(f16), .in_17(f17), .in_18(f18), .in_19(f19), .in_20(f20), .in_21(f21), .in_22(f22),
    .in_23(f23), .in_24(f24), .in_25(f25), .in_26(f26), .in_27(f27), .in_28(f28), .in_29(f29), .in_30(f30),
    .in_31(f31), .out(B));
  // also tied to GND on the sheet: {_0_q[0], _0_q[1], _0_q[2], _0_q[3], _0_q[4], _0_q[5], _0_q[6], _0_q[7], _0_q[8], _0_q[9], _0_q[10], _0_q[11], _0_q[12], _0_q[13], _0_q[14], _0_q[15], _0_q[16], _0_q[17], _0_q[18], _0_q[19], _0_q[20], _0_q[21], _0_q[22], _0_q[23], _0_q[24], _0_q[25], _0_q[26], _0_q[27], _0_q[28], _0_q[29], _0_q[30], _0_q[31]}

  // Other names for the same wires on the sheet: A_t[4:0] = rs1; B_t[4:0] = rs2; Crd[4:0] = rd; Cula[31:0] = ula
endmodule
