// Digital circuit registrador_dois.dig as structural Verilog
module registrador_dois (
  input  [4:0] rs1,
  input  [4:0] rs2,
  input  [4:0] rd,
  input  [31:0] ula,
  input  ck,
  input  W_reg,
  output [31:0] A,
  output [31:0] B
);

  wire C0, C1, C2, C3, C4, C5, C6, C7, C8, C9, C10, C11, C12, C13, C14, C15, C16, C17, C18, C19, C20, C21,
       C22, C23, C24, C25, C26, C27, C28, C29, C30, C31;
  wire [31:0] f1, f2, f3, f4, f5, f6, f7, f8, f9, f10, f11, f12, f13, f14, f15, f16, f17, f18, f19, f20, f21,
       f22, f23, f24, f25, f26, f27, f28, f29, f30, f31;

  Demultiplexer #(.Selector_Bits(5)) demultiplexer_1 (
    .sel(rd), .in(W_reg), .out_0(C0), .out_1(C1), .out_2(C2), .out_3(C3), .out_4(C4), .out_5(C5), .out_6(C6),
    .out_7(C7), .out_8(C8), .out_9(C9), .out_10(C10), .out_11(C11), .out_12(C12), .out_13(C13), .out_14(C14),
    .out_15(C15), .out_16(C16), .out_17(C17), .out_18(C18), .out_19(C19), .out_20(C20), .out_21(C21),
    .out_22(C22), .out_23(C23), .out_24(C24), .out_25(C25), .out_26(C26), .out_27(C27), .out_28(C28),
    .out_29(C29), .out_30(C30), .out_31(C31));
  Register #(.Bits(32)) register_1 (.D(ula), .C(ck), .en(C1), .Q(f1));
  Register #(.Bits(32)) register_2 (.D(ula), .C(ck), .en(C2), .Q(f2));
  Register #(.Bits(32)) register_3 (.D(ula), .C(ck), .en(C3), .Q(f3));
  Register #(.Bits(32)) register_4 (.D(ula), .C(ck), .en(C4), .Q(f4));
  Register #(.Bits(32)) register_5 (.D(ula), .C(ck), .en(C5), .Q(f5));
  Register #(.Bits(32)) register_6 (.D(ula), .C(ck), .en(C6), .Q(f6));
  Register #(.Bits(32)) register_7 (.D(ula), .C(ck), .en(C7), .Q(f7));
  Register #(.Bits(32)) register_8 (.D(ula), .C(ck), .en(C8), .Q(f8));
  Register #(.Bits(32)) register_9 (.D(ula), .C(ck), .en(C9), .Q(f9));
  Register #(.Bits(32)) register_10 (.D(ula), .C(ck), .en(C10), .Q(f10));
  Register #(.Bits(32)) register_11 (.D(ula), .C(ck), .en(C11), .Q(f11));
  Register #(.Bits(32)) register_12 (.D(ula), .C(ck), .en(C12), .Q(f12));
  Register #(.Bits(32)) register_13 (.D(ula), .C(ck), .en(C13), .Q(f13));
  Register #(.Bits(32)) register_14 (.D(ula), .C(ck), .en(C14), .Q(f14));
  Register #(.Bits(32)) register_15 (.D(ula), .C(ck), .en(C15), .Q(f15));
  Register #(.Bits(32)) register_16 (.D(ula), .C(ck), .en(C16), .Q(f16));
  Register #(.Bits(32)) register_17 (.D(ula), .C(ck), .en(C17), .Q(f17));
  Register #(.Bits(32)) register_18 (.D(ula), .C(ck), .en(C18), .Q(f18));
  Register #(.Bits(32)) register_19 (.D(ula), .C(ck), .en(C19), .Q(f19));
  Register #(.Bits(32)) register_20 (.D(ula), .C(ck), .en(C20), .Q(f20));
  Register #(.Bits(32)) register_21 (.D(ula), .C(ck), .en(C21), .Q(f21));
  Register #(.Bits(32)) register_22 (.D(ula), .C(ck), .en(C22), .Q(f22));
  Register #(.Bits(32)) register_23 (.D(ula), .C(ck), .en(C23), .Q(f23));
  Register #(.Bits(32)) register_24 (.D(ula), .C(ck), .en(C24), .Q(f24));
  Register #(.Bits(32)) register_25 (.D(ula), .C(ck), .en(C25), .Q(f25));
  Register #(.Bits(32)) register_26 (.D(ula), .C(ck), .en(C26), .Q(f26));
  Register #(.Bits(32)) register_27 (.D(ula), .C(ck), .en(C27), .Q(f27));
  Register #(.Bits(32)) register_28 (.D(ula), .C(ck), .en(C28), .Q(f28));
  Register #(.Bits(32)) register_29 (.D(ula), .C(ck), .en(C29), .Q(f29));
  Register #(.Bits(32)) register_30 (.D(ula), .C(ck), .en(C30), .Q(f30));
  Register #(.Bits(32)) register_31 (.D(ula), .C(ck), .en(C31), .Q(f31));
  Multiplexer #(.Selector_Bits(5), .Bits(32)) multiplexer_1 (
    .sel(rs1), .in_0({32{1'b0}}), .in_1(f1), .in_2(f2), .in_3(f3), .in_4(f4), .in_5(f5), .in_6(f6),
    .in_7(f7), .in_8(f8), .in_9(f9), .in_10(f10), .in_11(f11), .in_12(f12), .in_13(f13), .in_14(f14),
    .in_15(f15), .in_16(f16), .in_17(f17), .in_18(f18), .in_19(f19), .in_20(f20), .in_21(f21), .in_22(f22),
    .in_23(f23), .in_24(f24), .in_25(f25), .in_26(f26), .in_27(f27), .in_28(f28), .in_29(f29), .in_30(f30),
    .in_31(f31), .out(A));
  Multiplexer #(.Selector_Bits(5), .Bits(32)) multiplexer_2 (
    .sel(rs2), .in_0({32{1'b0}}), .in_1(f1), .in_2(f2), .in_3(f3), .in_4(f4), .in_5(f5), .in_6(f6),
    .in_7(f7), .in_8(f8), .in_9(f9), .in_10(f10), .in_11(f11), .in_12(f12), .in_13(f13), .in_14(f14),
    .in_15(f15), .in_16(f16), .in_17(f17), .in_18(f18), .in_19(f19), .in_20(f20), .in_21(f21), .in_22(f22),
    .in_23(f23), .in_24(f24), .in_25(f25), .in_26(f26), .in_27(f27), .in_28(f28), .in_29(f29), .in_30(f30),
    .in_31(f31), .out(B));

  // Other names for the same wires on the sheet: A_t[4:0] = rs1; B_t[4:0] = rs2; Crd[4:0] = rd; Cula[31:0] = ula
endmodule
