// Digital circuit somador.dig as structural Verilog
module somador (
  input  [31:0] A,
  input  B,
  input  [3:0] c_ula,
  output [31:0] Output,
  output zero
);

  wire Comparador_eq, Comparador_gt, Comparador_lt, Shift_right_out, xor_1_out;
  wire [31:0] and_1_out, or_1_out, Shift_Left_out, Sub_s, Sum_s;
  wire [31:1] undriven;

  Add #(.Bits(32)) Sum (.s(Sum_s));  // open: a, b, c_i, c_o
  Sub #(.Bits(32)) Sub (.s(Sub_s));  // open: a, b, c_i, c_o
  // And and_1 has open pins: In_1=open, In_2=open, out=and_1_out
  // XOr xor_1 has open pins: In_1=open, In_2=open, out=xor_1_out
  // Or or_1 has open pins: In_1=open, In_2=open, out=or_1_out
  BarrelShifter #(.Bits(32)) Shift_Left (.out(Shift_Left_out));  // open: in, shift
  BarrelShifter #(.direction("right")) Shift_right (.out(Shift_right_out));  // open: in, shift
  Comparator #(.Bits(32)) Comparador (.gt(Comparador_gt), .eq(Comparador_eq), .lt(Comparador_lt));  // open: a, b
  Multiplexer #(.Selector_Bits(4)) multiplexer_1 (
    .sel(c_ula), .in_0(Sum_s[0]), .in_1(Sub_s[0]), .in_2(and_1_out[0]), .in_3(xor_1_out), .in_4(or_1_out[0]),
    .in_5(Shift_Left_out[0]), .in_6(Shift_right_out), .in_7(Comparador_gt), .in_8(Comparador_eq),
    .in_9(Comparador_lt), .out(Output[0]));  // open: in_10, in_11, in_12, in_13, in_14, in_15
  Comparator #(.Bits(32)) comparator_1 (.a({undriven, 1'b0}), .b(Output), .eq(zero));  // open: gt, lt
  // Pins of 1 and 32 bits meet at Sum_s
  // Pins of 1 and 32 bits meet at Sub_s
  // Pins of 1 and 32 bits meet at and_1_out
  // Pins of 1 and 32 bits meet at or_1_out
  // Pins of 1 and 32 bits meet at Shift_Left_out
  // Pins of 1 and 32 bits meet at Output
  // Pins of 1 and 32 bits meet at {undriven, 1'b0}
endmodule
